// Logisim project CPU.circ as structural Verilog: 6 circuits, main circuit main
module main (
  input  in_1
);

  wire alu_8bit_1_zero, and_1_out, clock_1_out, control_r_lw_ori_beq_1_binvert,
       control_r_lw_ori_beq_1_branch, control_r_lw_ori_beq_1_regorimm, control_r_lw_ori_beq_1_regormem,
       control_r_lw_ori_beq_1_regwrite, multiplexer_2_out, multiplexer_3_out, multiplexer_4_out,
       multiplexer_5_out, or_1_out;
  wire [1:0] control_r_lw_ori_beq_1_operation;
  wire [4:0] rom_1_data;
  wire [7:0] adder_1_out, adder_2_out, alu_8bit_1_result, bit_extender_1_out, bit_extender_2_out,
       multiplexer_1_out, multiplexer_6_out, multiplexer_7_out, reg_file_1_read_data_1,
       reg_file_1_read_data_2, register_1_q, rom_2_data;
  wire [7:5] rom_1_data_2;

  Register register_1 (.D(multiplexer_1_out), .en(in_1), .clk(clock_1_out), .Q(register_1_q));  // open: clr
  Clock clock_1 (.out(clock_1_out));
  Adder adder_1 (.a(8'h1), .b(register_1_q), .out(adder_1_out));  // open: cin, cout
  assign bit_extender_1_out = {{3{rom_1_data[4]}}, rom_1_data};  // Bit_Extender bit_extender_1
  Multiplexer #(.width(8)) multiplexer_1 (
    .in0(adder_1_out), .in1(adder_2_out), .out(multiplexer_1_out), .sel(and_1_out));
  Adder adder_2 (.a(adder_1_out), .b(bit_extender_1_out), .out(adder_2_out));  // open: cin, cout
  ROM rom_1 (.addr(register_1_q), .data({rom_1_data_2, rom_1_data}));
  Multiplexer multiplexer_2 (.in0(rom_1_data[2]), .in1(rom_1_data[4]), .out(multiplexer_2_out), .sel(or_1_out));
  assign bit_extender_2_out = {{4{1'b0}}, rom_1_data[3:0]};  // Bit_Extender bit_extender_2
  control_R_lw_ori_beq control_r_lw_ori_beq_1 (
    .opcode({rom_1_data_2, rom_1_data[4:3]}), .RegWrite(control_r_lw_ori_beq_1_regwrite),
    .Operation(control_r_lw_ori_beq_1_operation), .Binvert(control_r_lw_ori_beq_1_binvert),
    .RegOrMem(control_r_lw_ori_beq_1_regormem), .RegOrimm(control_r_lw_ori_beq_1_regorimm),
    .Branch(control_r_lw_ori_beq_1_branch));
  Multiplexer multiplexer_3 (
    .in0(rom_1_data[1]), .in1(rom_1_data[4]), .out(multiplexer_3_out), .sel(control_r_lw_ori_beq_1_regorimm));
  Multiplexer multiplexer_4 (
    .in0(multiplexer_3_out), .in1(1'b0), .out(multiplexer_4_out), .sel(control_r_lw_ori_beq_1_branch));
  Multiplexer multiplexer_5 (
    .in0(rom_1_data[0]), .in1(1'b1), .out(multiplexer_5_out), .sel(control_r_lw_ori_beq_1_branch));
  or or_1 (or_1_out, control_r_lw_ori_beq_1_regormem, control_r_lw_ori_beq_1_regorimm);
  and and_1 (and_1_out, alu_8bit_1_zero, control_r_lw_ori_beq_1_branch);
  Multiplexer #(.width(8)) multiplexer_6 (
    .in0(alu_8bit_1_result), .in1(rom_2_data), .out(multiplexer_6_out), .sel(control_r_lw_ori_beq_1_regormem));
  reg_file reg_file_1 (
    .read_register_1(multiplexer_4_out), .read_register_2(multiplexer_5_out),
    .write_register(multiplexer_2_out), .write_data(multiplexer_6_out),
    .RegWrite(control_r_lw_ori_beq_1_regwrite), .clock(clock_1_out), .read_data_1(reg_file_1_read_data_1),
    .read_data_2(reg_file_1_read_data_2));
  Multiplexer #(.width(8)) multiplexer_7 (
    .in0(reg_file_1_read_data_2), .in1(bit_extender_2_out), .out(multiplexer_7_out),
    .sel(control_r_lw_ori_beq_1_regorimm));
  ALU_8bit alu_8bit_1 (
    .operation(control_r_lw_ori_beq_1_operation), .carryin(control_r_lw_ori_beq_1_binvert),
    .binvert(control_r_lw_ori_beq_1_binvert), .a(reg_file_1_read_data_1), .b(multiplexer_7_out),
    .Result(alu_8bit_1_result), .zero(alu_8bit_1_zero));  // open: Carryout
  ROM rom_2 (.addr(bit_extender_2_out), .data(rom_2_data));

  // Notes on the sheet:
  //   無控制電路                  machine code                      result
  //   00  nop                             00                                        $0=0, $1=0
  //   01  lw $0,Mem[3]              43                                        $0=5, $1=0
  //   02  lw $1,Mem[6]              56                                        $0=5, $1=2
  //   03  or $1,$0,$1                  2d                                        $0=5, $1=7
  //   04  add $0,$0,$0               30                                         $0=a, $1=7
  //   05  and $1,$0,$1               25                                         $0=a, $1=2
  //   06  sub $1,$0,$1               3d                                         $0=a, $1=8
  //   07  ori $1, 2                      b2                                         $0=a, $1=a
  //   08  beq -5                         fb                                         $0=a, $1=a
  //   暫存器預設值: $0=0, $1=0    Data Memory     [3] = 5, [6] = 2
  //   contents of rom_1 (hex, n*v repeats v):
  //   0 43 56 2d 30 25 3d b2 fb
  //   $0=14, $1=a
  //   $0=14, $1=0
  //    $0=14, $1=14
  //    $0=14, $1=16
  //   姓名: 趙竟程           學號:111321033
  //   rd
  //   branch
  //   ori
  //   branch
  //   RegOrimm
  //   RegOrMem
  //   contents of rom_2 (hex, n*v repeats v):
  //   0 0 0 5 0 0 2
endmodule

module reg_file (
  input  read_register_1,
  input  read_register_2,
  input  write_register,
  input  [7:0] write_data,
  input  RegWrite,
  input  clock,
  output [7:0] read_data_1,
  output [7:0] read_data_2
);

  wire and_1_out, and_2_out, decoder_1_out0, decoder_1_out1, undriven;
  wire [7:0] reg_0_q, reg_1_q;

  Decoder decoder_1 (.out0(decoder_1_out0), .out1(decoder_1_out1), .sel(write_register), .en(undriven));
  and and_1 (and_1_out, decoder_1_out0, RegWrite);
  and and_2 (and_2_out, decoder_1_out1, RegWrite);
  Register reg_0 (.D(write_data), .en(and_1_out), .clk(clock), .Q(reg_0_q), .clr(1'b0));
  Register reg_1 (.D(write_data), .en(and_2_out), .clk(clock), .Q(reg_1_q), .clr(1'b0));
  Multiplexer #(.width(8)) multiplexer_1 (.in0(reg_0_q), .in1(reg_1_q), .out(read_data_1), .sel(read_register_1));
  Multiplexer #(.width(8)) multiplexer_2 (.in0(reg_0_q), .in1(reg_1_q), .out(read_data_2), .sel(read_register_2));
endmodule

module ALU_1bit (
  input  a,
  input  b,
  input  CarryIn,
  input  Binvert,
  input  Less,
  input  [1:0] Operation,
  output Result,
  output CarryOut
);

  wire adder_1_out, and_1_out, multiplexer_1_out, not_1_out, or_1_out;

  Multiplexer multiplexer_1 (.in0(b), .in1(not_1_out), .out(multiplexer_1_out), .sel(Binvert));
  not not_1 (not_1_out, b);
  and and_1 (and_1_out, a, b);
  or or_1 (or_1_out, a, b);
  Adder #(.width(1)) adder_1 (.a(a), .b(multiplexer_1_out), .out(adder_1_out), .cin(CarryIn), .cout(CarryOut));
  Multiplexer #(.select(2)) multiplexer_2 (
    .in0(and_1_out), .in1(or_1_out), .in2(adder_1_out), .in3(Less), .out(Result), .sel(Operation));
endmodule

module ALU_1bit_MSB (
  input  a,
  input  b,
  input  Binvert,
  input  carryin,
  input  less,
  input  [1:0] operation,
  output result,
  output carryout,
  output set
);

  wire adder_1_out, and_1_out, and_2_out, and_3_out, multiplexer_1_out, not_1_out, not_2_out, or_1_out,
       overflow_out;

  Multiplexer multiplexer_1 (.in0(b), .in1(not_1_out), .out(multiplexer_1_out), .sel(Binvert));
  not not_1 (not_1_out, b);
  and and_1 (and_1_out, a, multiplexer_1_out);
  or or_1 (or_1_out, a, multiplexer_1_out);
  Adder #(.width(1)) adder_1 (.a(a), .b(multiplexer_1_out), .out(adder_1_out), .cin(carryin), .cout(carryout));
  not not_2 (not_2_out, overflow_out);
  xor overflow (overflow_out, carryin, carryout);
  Multiplexer #(.select(2)) multiplexer_2 (
    .in0(and_1_out), .in1(or_1_out), .in2(adder_1_out), .in3(less), .out(result), .sel(operation));
  and and_2 (and_2_out, adder_1_out, not_2_out);
  and and_3 (and_3_out, overflow_out, a);
  or or_2 (set, and_2_out, and_3_out);
endmodule

module ALU_8bit (
  input  [1:0] operation,
  input  carryin,
  input  binvert,
  input  [7:0] a,
  input  [7:0] b,
  output [7:0] Result,
  output Carryout,
  output zero
);

  wire alu_1bit_1_carryout, alu_1bit_2_carryout, alu_1bit_3_carryout, alu_1bit_4_carryout,
       alu_1bit_5_carryout, alu_1bit_6_carryout, alu_1bit_7_carryout, alu_1bit_msb_1_set, or_1_out;

  ALU_1bit alu_1bit_1 (
    .a(a[0]), .b(b[0]), .CarryIn(carryin), .Binvert(binvert), .Less(alu_1bit_msb_1_set),
    .Operation(operation), .Result(Result[0]), .CarryOut(alu_1bit_1_carryout));
  ALU_1bit alu_1bit_2 (
    .a(a[1]), .b(b[1]), .CarryIn(alu_1bit_1_carryout), .Binvert(binvert), .Less(1'b0), .Operation(operation),
    .Result(Result[1]), .CarryOut(alu_1bit_2_carryout));
  ALU_1bit alu_1bit_3 (
    .a(a[2]), .b(b[2]), .CarryIn(alu_1bit_2_carryout), .Binvert(binvert), .Less(1'b0), .Operation(operation),
    .Result(Result[2]), .CarryOut(alu_1bit_3_carryout));
  ALU_1bit alu_1bit_4 (
    .a(a[3]), .b(b[3]), .CarryIn(alu_1bit_3_carryout), .Binvert(binvert), .Less(1'b0), .Operation(operation),
    .Result(Result[3]), .CarryOut(alu_1bit_4_carryout));
  ALU_1bit alu_1bit_5 (
    .a(a[4]), .b(b[4]), .CarryIn(alu_1bit_4_carryout), .Binvert(binvert), .Less(1'b0), .Operation(operation),
    .Result(Result[4]), .CarryOut(alu_1bit_5_carryout));
  ALU_1bit alu_1bit_6 (
    .a(a[5]), .b(b[5]), .CarryIn(alu_1bit_5_carryout), .Binvert(binvert), .Less(1'b0), .Operation(operation),
    .Result(Result[5]), .CarryOut(alu_1bit_6_carryout));
  ALU_1bit alu_1bit_7 (
    .a(a[6]), .b(b[6]), .CarryIn(alu_1bit_6_carryout), .Binvert(binvert), .Less(1'b0), .Operation(operation),
    .Result(Result[6]), .CarryOut(alu_1bit_7_carryout));
  ALU_1bit_MSB alu_1bit_msb_1 (
    .a(a[7]), .b(b[7]), .Binvert(binvert), .carryin(alu_1bit_7_carryout), .less(1'b0), .operation(operation),
    .result(Result[7]), .carryout(Carryout), .set(alu_1bit_msb_1_set));
  or or_1 (or_1_out, Result[0], Result[1], Result[2], Result[3], Result[4], Result[5], Result[6], Result[7]);
  not not_1 (zero, or_1_out);
endmodule

module control_R_lw_ori_beq (
  input  [4:0] opcode,
  output RegWrite,
  output [1:0] Operation,
  output Binvert,
  output RegOrMem,
  output RegOrimm,
  output Branch
);

  wire and_1_out, and_2_out, and_3_out, and_4_out, and_5_out, and_6_out, not_1_out, not_2_out, not_3_out,
       not_4_out;

  not not_1 (not_1_out, opcode[4]);
  not not_2 (not_2_out, opcode[3]);
  not not_3 (not_3_out, opcode[2]);
  not not_4 (not_4_out, opcode[1]);
  and and_1 (and_1_out, not_2_out, opcode[2]);
  or or_1 (RegWrite, and_1_out, and_2_out);
  and and_2 (and_2_out, opcode[3], not_3_out);
  and and_3 (and_3_out, not_1_out, opcode[1]);
  or or_2 (Operation[1], and_3_out, opcode[3]);
  and and_4 (and_4_out, opcode[4], not_2_out);
  or or_3 (Operation[0], and_4_out, and_5_out);
  and and_5 (and_5_out, not_2_out, not_4_out, opcode[0]);
  and and_6 (and_6_out, not_1_out, opcode[1], opcode[0]);
  or or_4 (Binvert, and_6_out, opcode[3]);
  and and_7 (RegOrimm, opcode[4], not_2_out);
  and and_8 (Branch, opcode[3], opcode[2]);

  assign RegOrMem = opcode[3];
endmodule
